# Fritzing sketch DistanceSensorGate (saved by Fritzing 1.0.4)
breadboards: 1

parts:
  Microcontroller_1 = Arduino Uno (Rev3)
  Sensor_1 = HC-SR04 Ultrasonic Distance Sensor [part_number=HC-SR04 mn="Ultrasonic Distance Sensor"]
  LED1 = LED - 5mm [color="Blue (505nm)" current=0.030A package="5 mm [THT]"]
  R1 = Resistor [tolerance=±5% resistance=220 package="1206 [SMD]"]
  J1 = Piezo Speaker [part_number="Piezo buzzer"]

nets:
  N1: Microcontroller_1.D8, J1.pin2
  N2: Microcontroller_1.D9_PWM, R1.Pin_1
  N3: Microcontroller_1.D10_PWM/SS, Sensor_1.TRIG
  N4: Microcontroller_1.D11_PWM/MOSI, Sensor_1.ECHO
  GND: Microcontroller_1.GND, Sensor_1.GND, LED1.cathode, J1.pin1
  5V: Microcontroller_1.5V, Sensor_1.VCC
  N5: LED1.anode, R1.Pin_0
